# Fritzing sketch accel (saved by Fritzing 0.8.3b)
circuit board: 9.2cm x 4.2cm
breadboards: 1

parts:
  3-Axis_Accelerometer1 = 3-Axis Accelerometer Breakout - MMA8452Q
  R1 = Resistor [tolerance=±5% resistance=220 package=THT]
  U1 = atmega328 [package=dip]
  R2 = Resistor [tolerance=±5% resistance=220 package=THT]
  R3 = Resistor [tolerance=±5% resistance=220 package=THT]
  R4 = Resistor [tolerance=±5% resistance=220 package=THT]
  R5 = Resistor [tolerance=±5% resistance=220 package=THT]
  R6 = Resistor [tolerance=±5% resistance=220 package=THT]
  R7 = Resistor [tolerance=±5% resistance=220 package=THT]
  R9 = Resistor [tolerance=±5% resistance=220 package=THT]
  R10 = Resistor [tolerance=±5% resistance=220 package=THT]
  R11 = Resistor [tolerance=±5% resistance=220 package=THT]
  R12 = Resistor [tolerance=±5% resistance=220 package=THT]
  R13 = Resistor [tolerance=±5% resistance=220 package=THT]
  LED1 = LED - 5mm [color="White (6500K)" package="5 mm [THT]"]
  LED2 = LED - 5mm [color="White (6500K)" package="5 mm [THT]"]
  LED3 = LED - 5mm [color="White (6500K)" package="5 mm [THT]"]
  LED4 = LED - 5mm [color="White (6500K)" package="5 mm [THT]"]
  LED5 = LED - 5mm [color="White (6500K)" package="5 mm [THT]"]
  LED6 = LED - 5mm [color="White (6500K)" package="5 mm [THT]"]
  LED7 = LED - 5mm [color="White (6500K)" package="5 mm [THT]"]
  LED8 = LED - 5mm [color="White (6500K)" package="5 mm [THT]"]
  LED9 = LED - 5mm [color="Blue (505nm)" package="5 mm [THT]"]
  LED10 = LED - 5mm [color="White (6500K)" package="5 mm [THT]"]
  LED11 = LED - 5mm [color="White (6500K)" package="5 mm [THT]"]
  LED12 = LED - 5mm [color="White (6500K)" package="5 mm [THT]"]
  J1 = AVR ISP 6 Pin [package=2x3-ns]
  VCC1 = Battery
  R8 = Resistor [tolerance=±5% resistance=220 package=THT]

nets:
  N1: 3-Axis_Accelerometer1.3.3V, R1.Pin_1
  N2: 3-Axis_Accelerometer1.SDA, U1.A4
  N3: 3-Axis_Accelerometer1.SCL, U1.A5
  N4: 3-Axis_Accelerometer1.I2, U1.A3
  N5: 3-Axis_Accelerometer1.I1, U1.A2
  N6: 3-Axis_Accelerometer1.GND, U1.GND#7, LED1.cathode, LED2.cathode, LED3.cathode, LED4.cathode, LED5.cathode, LED6.cathode, LED7.cathode, LED8.cathode, LED9.cathode, LED10.cathode, LED11.cathode, LED12.cathode, VCC1.-
  N7: R1.Pin_0, U1.VCC, VCC1.+
  N8: U1.RESET, J1.5
  N9: U1.D2, R2.Pin_0
  N10: U1.D3_(PWM), R3.Pin_0
  N11: U1.D4, R4.Pin_0
  N12: U1.D5_(PWM), R5.Pin_0
  N13: U1.D6_(PWM), R6.Pin_0
  N14: U1.D7, R7.Pin_0
  N15: U1.D8, R8.Pin_0
  N16: U1.D9_(PWM), R9.Pin_0
  N17: U1.D10_(PWM), R10.Pin_0
  N18: U1.D11_(PWM), R11.Pin_0, J1.4
  N19: U1.D12, R12.Pin_0, J1.1
  N20: U1.D13, R13.Pin_0, J1.3
  N21: R2.Pin_1, LED1.anode
  N22: R3.Pin_1, LED2.anode
  N23: R4.Pin_1, LED3.anode
  N24: R5.Pin_1, LED4.anode
  N25: R6.Pin_1, LED5.anode
  N26: R7.Pin_1, LED6.anode
  N27: R9.Pin_1, LED8.anode
  N28: R10.Pin_1, LED9.anode
  N29: R11.Pin_1, LED10.anode
  N30: R12.Pin_1, LED11.anode
  N31: R13.Pin_1, LED12.anode
  N32: LED7.anode, R8.Pin_1
